// Digital circuit 8-BitRegister.dig as structural Verilog
module _8_BitRegister (
  input  [7:0] D,
  input  CLK,
  input  EN,
  input  CLR,
  output [7:0] Q
);

  wire and_1_out, and_2_out, and_3_out, and_4_out, and_5_out, and_6_out, and_7_out, and_8_out,
       multiplexer_1_out, multiplexer_2_out, multiplexer_3_out, multiplexer_4_out, multiplexer_5_out,
       multiplexer_6_out, multiplexer_7_out, multiplexer_8_out, not_1_out, not_2_out, not_3_out, not_4_out,
       not_5_out, not_6_out, not_7_out, not_8_out;

  not not_1 (not_1_out, CLR);
  not not_2 (not_2_out, CLR);
  not not_3 (not_3_out, CLR);
  not not_4 (not_4_out, CLR);
  not not_5 (not_5_out, CLR);
  not not_6 (not_6_out, CLR);
  not not_7 (not_7_out, CLR);
  not not_8 (not_8_out, CLR);
  and and_1 (and_1_out, Q[7], not_1_out);
  and and_2 (and_2_out, Q[6], not_2_out);
  and and_3 (and_3_out, Q[5], not_3_out);
  and and_4 (and_4_out, Q[4], not_4_out);
  and and_5 (and_5_out, Q[3], not_5_out);
  and and_6 (and_6_out, Q[2], not_6_out);
  and and_7 (and_7_out, Q[1], not_7_out);
  and and_8 (and_8_out, Q[0], not_8_out);
  Multiplexer multiplexer_1 (.sel(EN), .in_0(and_1_out), .in_1(D[7]), .out(multiplexer_1_out));
  Multiplexer multiplexer_2 (.sel(EN), .in_0(and_2_out), .in_1(D[6]), .out(multiplexer_2_out));
  Multiplexer multiplexer_3 (.sel(EN), .in_0(and_3_out), .in_1(D[5]), .out(multiplexer_3_out));
  Multiplexer multiplexer_4 (.sel(EN), .in_0(and_4_out), .in_1(D[4]), .out(multiplexer_4_out));
  Multiplexer multiplexer_5 (.sel(EN), .in_0(and_5_out), .in_1(D[3]), .out(multiplexer_5_out));
  Multiplexer multiplexer_6 (.sel(EN), .in_0(and_6_out), .in_1(D[2]), .out(multiplexer_6_out));
  Multiplexer multiplexer_7 (.sel(EN), .in_0(and_7_out), .in_1(D[1]), .out(multiplexer_7_out));
  Multiplexer multiplexer_8 (.sel(EN), .in_0(and_8_out), .in_1(D[0]), .out(multiplexer_8_out));
  D_FF d_ff_1 (.D(multiplexer_1_out), .C(CLK), .Q(Q[7]));  // open: nQ
  D_FF d_ff_2 (.D(multiplexer_2_out), .C(CLK), .Q(Q[6]));  // open: nQ
  D_FF d_ff_3 (.D(multiplexer_3_out), .C(CLK), .Q(Q[5]));  // open: nQ
  D_FF d_ff_4 (.D(multiplexer_4_out), .C(CLK), .Q(Q[4]));  // open: nQ
  D_FF d_ff_5 (.D(multiplexer_5_out), .C(CLK), .Q(Q[3]));  // open: nQ
  D_FF d_ff_6 (.D(multiplexer_6_out), .C(CLK), .Q(Q[2]));  // open: nQ
  D_FF d_ff_7 (.D(multiplexer_7_out), .C(CLK), .Q(Q[1]));  // open: nQ
  D_FF d_ff_8 (.D(multiplexer_8_out), .C(CLK), .Q(Q[0]));  // open: nQ
endmodule
