// Digital circuit BitRegisterWithSet.dig as structural Verilog
module BitRegisterWithSet (
  input  [7:0] D,
  input  CLOCK,
  input  EN,
  input  CLEAR,
  input  SetFF,
  output [7:0] Q
);

  wire and_1_out, and_2_out, and_3_out, and_4_out, and_5_out, and_6_out, and_7_out, and_8_out,
       multiplexer_2_out, multiplexer_3_out, multiplexer_4_out, multiplexer_5_out, multiplexer_6_out,
       multiplexer_7_out, multiplexer_8_out, multiplexer_9_out, not_1_out, not_2_out, not_3_out, not_4_out,
       not_5_out, not_6_out, not_7_out, not_8_out, or_1_out;
  wire [7:0] multiplexer_1_out;

  or or_1 (or_1_out, SetFF, EN);
  Multiplexer #(.Bits(8)) multiplexer_1 (.sel(SetFF), .in_0(D), .in_1({8{1'b1}}), .out(multiplexer_1_out));
  not not_1 (not_1_out, CLEAR);
  not not_2 (not_2_out, CLEAR);
  not not_3 (not_3_out, CLEAR);
  not not_4 (not_4_out, CLEAR);
  not not_5 (not_5_out, CLEAR);
  not not_6 (not_6_out, CLEAR);
  not not_7 (not_7_out, CLEAR);
  not not_8 (not_8_out, CLEAR);
  and and_1 (and_1_out, Q[7], not_1_out);
  and and_2 (and_2_out, Q[6], not_2_out);
  and and_3 (and_3_out, Q[5], not_3_out);
  and and_4 (and_4_out, Q[4], not_4_out);
  and and_5 (and_5_out, Q[3], not_5_out);
  and and_6 (and_6_out, Q[2], not_6_out);
  and and_7 (and_7_out, Q[1], not_7_out);
  and and_8 (and_8_out, Q[0], not_8_out);
  Multiplexer multiplexer_2 (.sel(or_1_out), .in_0(and_1_out), .in_1(multiplexer_1_out[7]), .out(multiplexer_2_out));
  Multiplexer multiplexer_3 (.sel(or_1_out), .in_0(and_2_out), .in_1(multiplexer_1_out[6]), .out(multiplexer_3_out));
  Multiplexer multiplexer_4 (.sel(or_1_out), .in_0(and_3_out), .in_1(multiplexer_1_out[5]), .out(multiplexer_4_out));
  Multiplexer multiplexer_5 (.sel(or_1_out), .in_0(and_4_out), .in_1(multiplexer_1_out[4]), .out(multiplexer_5_out));
  Multiplexer multiplexer_6 (.sel(or_1_out), .in_0(and_5_out), .in_1(multiplexer_1_out[3]), .out(multiplexer_6_out));
  Multiplexer multiplexer_7 (.sel(or_1_out), .in_0(and_6_out), .in_1(multiplexer_1_out[2]), .out(multiplexer_7_out));
  Multiplexer multiplexer_8 (.sel(or_1_out), .in_0(and_7_out), .in_1(multiplexer_1_out[1]), .out(multiplexer_8_out));
  Multiplexer multiplexer_9 (.sel(or_1_out), .in_0(and_8_out), .in_1(multiplexer_1_out[0]), .out(multiplexer_9_out));
  D_FF d_ff_1 (.D(multiplexer_2_out), .C(CLOCK), .Q(Q[7]));  // open: nQ
  D_FF d_ff_2 (.D(multiplexer_3_out), .C(CLOCK), .Q(Q[6]));  // open: nQ
  D_FF d_ff_3 (.D(multiplexer_4_out), .C(CLOCK), .Q(Q[5]));  // open: nQ
  D_FF d_ff_4 (.D(multiplexer_5_out), .C(CLOCK), .Q(Q[4]));  // open: nQ
  D_FF d_ff_5 (.D(multiplexer_6_out), .C(CLOCK), .Q(Q[3]));  // open: nQ
  D_FF d_ff_6 (.D(multiplexer_7_out), .C(CLOCK), .Q(Q[2]));  // open: nQ
  D_FF d_ff_7 (.D(multiplexer_8_out), .C(CLOCK), .Q(Q[1]));  // open: nQ
  D_FF d_ff_8 (.D(multiplexer_9_out), .C(CLOCK), .Q(Q[0]));  // open: nQ
endmodule
