// Digital circuit GPR.dig as structural Verilog
module GPR (
  input  clk,
  input  [1:0] STORE,
  input  CLEAR,
  input  [7:0] D,
  input  [1:0] LOAD,
  output [7:0] out_2
);

  wire decoder_1_out_0, decoder_1_out_1, decoder_1_out_2, decoder_1_out_3;
  wire [7:0] R_0_q, R_1_q, R_2_q, R_3_q;

  Decoder #(.Selector_Bits(2)) decoder_1 (
    .sel(STORE), .out_0(decoder_1_out_0), .out_1(decoder_1_out_1), .out_2(decoder_1_out_2),
    .out_3(decoder_1_out_3));
  _8_BitRegister R_0 (.D(D), .CLK(clk), .EN(decoder_1_out_0), .CLR(CLEAR), .Q(R_0_q));
  _8_BitRegister R_1 (.D(D), .CLK(clk), .EN(decoder_1_out_1), .CLR(CLEAR), .Q(R_1_q));
  _8_BitRegister R_2 (.D(D), .CLK(clk), .EN(decoder_1_out_2), .CLR(CLEAR), .Q(R_2_q));
  _8_BitRegister R_3 (.D(D), .CLK(clk), .EN(decoder_1_out_3), .CLR(CLEAR), .Q(R_3_q));
  Multiplexer #(.Selector_Bits(2), .Bits(8)) multiplexer_1 (
    .sel(LOAD), .in_0(R_0_q), .in_1(R_1_q), .in_2(R_2_q), .in_3(R_3_q), .out(out_2));
endmodule
