// Digital circuit IR.dig as structural Verilog
module IR (
  input  [7:0] D,
  input  SEL,
  input  LOAD,
  input  CLOCK,
  input  CLEAR,
  input  [7:0] D_s,
  output [7:0] Q
);

  wire [7:0] multiplexer_1_out;

  Multiplexer #(.Bits(8)) multiplexer_1 (.sel(SEL), .in_0(D), .in_1(D_s), .out(multiplexer_1_out));
  _8_BitRegister _8_bitregister_1 (.D(multiplexer_1_out), .CLK(CLOCK), .EN(LOAD), .CLR(CLEAR), .Q(Q));
endmodule
