// Digital circuit PC-3.dig as structural Verilog
module PC_3 (
  input  [7:0] D,
  input  INC,
  input  LD,
  input  CLK,
  input  RST,
  output [7:0] PC_Out
);

  wire [7:0] add_1_s, multiplexer_1_out;

  Add #(.Bits(8)) add_1 (.a(PC_Out), .b(8'h1), .c_i(1'b0), .s(add_1_s));  // open: c_o
  Multiplexer #(.Bits(8)) multiplexer_1 (.sel(INC), .in_0(D), .in_1(add_1_s), .out(multiplexer_1_out));
  _8_BitRegister _8_bitregister_1 (.D(multiplexer_1_out), .CLK(CLK), .EN(LD), .CLR(RST), .Q(PC_Out));
endmodule
